# Fritzing sketch schematics (saved by Fritzing 0.9.3b)
breadboards: 2

parts:
  M1 = DOIT Esp32 DevKit v1 (30 pins long, 11 pins width) [part_number=ESP32S-PIN30]
  J1 = Buzzer
  R1 = Resistor [tolerance=±5% resistance=220 package="0402 [SMD]"]
  R2 = Resistor [tolerance=±5% resistance=220 package=THT]
  R3 = Resistor [tolerance=±5% resistance=220 package=THT]
  R4 = Resistor [tolerance=±5% resistance=220 package=THT]
  LED1 = RGB LED (com. cathode, rgb) [package="5 mm [THT]"]
  LED2 = smd LED [color="Red (633nm)" package="0805 [SMD]"]
  LED3 = LED - 3mm [color="Red (633nm)" package="3 mm [THT]"]
  Part1 = SRF05 Ultrasonic Rangefinder
  IR_Receiver1 = IR_Receiver
  S1 = H-Bridge with L298N
  M2 = Getriebemotor  # not connected
  M4 = Getriebemotor  # not connected
  M5 = Getriebemotor  # not connected
  M6 = Getriebemotor  # not connected

nets:
  GND: M1.GND, S1.GND
  N1: M1.D15, Part1.Trig
  N2: M1.D2, Part1.Echo
  N3: M1.D4, S1.IN3
  N4: M1.D5, S1.IN4
  N5: M1.D18, S1.IN2
  N6: M1.D19, S1.IN1
  N7: M1.D21, IR_Receiver1.OUT
  N8: M1.D22, S1.ENB
  N9: M1.D23, S1.ENA
  N10: M1.D35, LED3.anode
  N11: M1.D25, LED2.anode
  N12: M1.D27, R3.Pin_1
  N13: M1.D14, R4.Pin_1
  N14: M1.D12, R2.Pin_1
  N15: M1.D13, R1.Pin_1
  VIN: M1.VIN, S1.5V
  GND_2: J1.pin1, Part1.GND, IR_Receiver1.GND
  N16: J1.pin2, R1.Pin_0
  N17: R2.Pin_0, LED1.red_anode
  N18: R3.Pin_0, LED1.blue_anode
  N19: R4.Pin_0, LED1.common_cathode
  VCC: LED1.green_anode, Part1.VCC, IR_Receiver1.VCC

custom parts:
  DOIT Esp32 DevKit v1 (30 pins long, 11 pins width): The DOIT Esp32 DevKit v1 is one of the development board created by DOIT to evaluate the ESP-WROOM-32 module. It is based on the ESP32 microcontroller that boasts Wifi, Bluetooth, Ethernet and Low Power support all in a single chip. (vanepp) made breadboard work, adjusted pin numbering and labels and reduced size of schematic and cleaned up pcb. This chip is 30pins long (2 x15) and 11 pins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
  Buzzer: Fixed frequency buzzer
  IR_Receiver: 赤外線受信モジュール GP1UXC41QS
  H-Bridge with L298N: h-bridge
